# Fritzing sketch electronic sketch 1 (saved by Fritzing 0.9.3b)

parts:
  Arduino = Arduino Uno (Rev3)
  Potentiometer_(6V) = LM2931_FIXED [package=dpak]
  Little_finger = Basic Servo
  Ring_finger = Basic Servo
  Middle_finger = Basic Servo
  Index_finger = Basic Servo

nets:
  N1: Arduino.D9_PWM, Ring_finger.pulse
  N2: Arduino.D11_PWM/MOSI, Little_finger.pulse
  GND: Arduino.GND, Potentiometer_(6V).GND, Little_finger.gnd, Ring_finger.gnd, Middle_finger.gnd, Index_finger.gnd
  N3: Arduino.D3_PWM, Index_finger.pulse
  N4: Arduino.D5_PWM, Middle_finger.pulse
  N5: Potentiometer_(6V).VOUT, Index_finger.vcc
